# Fritzing sketch circuit (saved by Fritzing 0.9.4)
breadboards: 1

parts:
  부품1 = Arduino Uno (Rev3)
  J1 = Basic Servo
  R1 = Resistor [tolerance=±5% resistance=220 package="0402 [SMD]"]
  LED1 = LED - 5mm [color="Red (633nm)" package="5 mm [THT]"]
  LED2 = LED - 5mm [color="Red (633nm)" package="5 mm [THT]"]
  R2 = Resistor [tolerance=±5% resistance=220 package="0402 [SMD]"]

nets:
  N1: 부품1.D2, R1.Pin_1
  N2: 부품1.D3_PWM, R2.Pin_1
  N3: 부품1.D6_PWM, J1.pulse
  5V: 부품1.5V, J1.vcc
  GND: 부품1.GND, J1.gnd, LED1.cathode, LED2.cathode
  N4: R1.Pin_0, LED1.anode
  N5: LED2.anode, R2.Pin_0
