# Fritzing sketch [수정] circuit (saved by Fritzing 0.9.4)
breadboards: 1

parts:
  부품1 = Arduino Uno (Rev3)
  J1 = Basic Servo
  HC-SR04_Sensor_1 = HC-SR04 Ultrasonic Distance Sensor

nets:
  N1: 부품1.D8, HC-SR04_Sensor_1.TRIG
  N2: 부품1.D9_PWM, HC-SR04_Sensor_1.ECHO
  N3: 부품1.D7, J1.pulse
  VCC: 부품1.5V, J1.vcc, HC-SR04_Sensor_1.VCC
  GND: 부품1.GND, J1.gnd, HC-SR04_Sensor_1.GND
